# Fritzing sketch Untitled Sketch (saved by Fritzing 0.9.3b)

parts:
  Part1 = Arduino Nano (Rev3.0)
  Part2 = Bluetooth HC-05 Macho
  M1 = DC Motor
  M2 = DC Motor
  U2 = L298_BRIDGE_DRIVER [package=powerso20]
  VCC1 = Battery
  LM1 = RioRand LM2596

nets:
  N1: Part1.D1/TX, Part2.TXD
  N2: Part1.D0/RX, Part2.RXD
  GND: Part1.GND, Part2.GND, LM1.Pin_3
  N3: Part1.VIN, U2.VS, LM1.Pin_2
  3V3: Part1.3V3, Part2.VCC
  N4: M1.pin_1, U2.OUT2
  N5: M1.pin_2, U2.OUT1
  N6: M2.pin_1, U2.OUT3
  N7: M2.pin_2, U2.OUT4
  N8: VCC1.-, LM1.Pin_0
  N9: VCC1.+, LM1.Pin_1
